# Fritzing sketch PCB_design (saved by Fritzing 0.9.3b)
circuit board: 9.906cm x 7.62cm

parts:
  2 = smd LED [color="Red (633nm)" package="0603 [SMD]"]
  1 = smd LED [color="Red (633nm)" package="0603 [SMD]"]
  0 = smd LED [color="Red (633nm)" package="0603 [SMD]"]
  CZ2 = Pushbutton [package="[SMD]"]
  Phase = Pushbutton [package="[SMD]"]
  Error = Pushbutton [package="[SMD]"]
  Swap = Pushbutton [package="[SMD]"]
  CZ1 = Pushbutton [package="[SMD]"]
  Measure = Pushbutton [package="[SMD]"]
  R8 = Resistor [tolerance=±5% resistance=220 package="0603 [SMD]"]
  R4 = Resistor [tolerance=±5% resistance=220 package="0603 [SMD]"]
  R3 = Resistor [tolerance=±5% resistance=220 package="0603 [SMD]"]
  R1 = Resistor [tolerance=±5% resistance=220 package="0603 [SMD]"]
  U2 = RJ45 Jack [package=rj45-8]
  ATTiny4313 = ATTiny4313 [chip_label=IC package=SO(w)]
  Activity = smd LED [color="Green (565nm)" package="0603 [SMD]"]
  U1 = RJ45 Jack [package=rj45-8]
  C1 = Ceramic Capacitor [capacitance=100nF package="100 mil [THT, multilayer]"]

nets:
  N1: 2.cathode, 1.cathode, 0.cathode, R1.Pin_1
  N2: 2.anode, ATTiny4313.14
  N3: 1.anode, ATTiny4313.15
  N4: 0.anode, ATTiny4313.16
  N5: CZ2.Pin_1, CZ2.Pin_2, ATTiny4313.9
  N6: CZ2.Pin_3, CZ2.Pin_4, Phase.Pin_3, Phase.Pin_4, Error.Pin_3, Error.Pin_4, Swap.Pin_1, Swap.Pin_2, CZ1.Pin_1, CZ1.Pin_2, Measure.Pin_3, Measure.Pin_4, R4.Pin_1, R1.Pin_0, ATTiny4313.10, C1.0
  N7: Phase.Pin_1, Phase.Pin_2, ATTiny4313.8
  N8: Error.Pin_1, Error.Pin_2, ATTiny4313.7
  N9: Swap.Pin_3, Swap.Pin_4, ATTiny4313.6
  N10: CZ1.Pin_3, CZ1.Pin_4, ATTiny4313.2
  N11: Measure.Pin_1, Measure.Pin_2, ATTiny4313.11
  N12: R8.Pin_0, R8.Pin_1, U2.3, ATTiny4313.4
  N13: R4.Pin_0, Activity.cathode
  N14: R3.Pin_0, ATTiny4313.5
  N15: R3.Pin_1, U1.3
  N16: U2.1, ATTiny4313.3
  N17: U2.2, ATTiny4313.1
  N18: U2.4, ATTiny4313.20, C1.1
  N19: U2.5, ATTiny4313.17
  N20: U2.6, ATTiny4313.19
  N21: U2.8, ATTiny4313.18
  N22: ATTiny4313.12, U1.1
  N23: ATTiny4313.13, Activity.anode

custom parts:
  Pushbutton: A generic pushbutton.
